// Digital circuit Clocked D Latch.dig as structural Verilog
module Clocked_D_Latch (
  input  clk,
  input  D,
  output Q,
  output nQ
);

  wire nand_1_out, nand_2_out;

  nand nand_1 (nand_1_out, D, clk);
  nand nand_2 (nand_2_out, nand_1_out, clk);
  nand nand_3 (Q, nand_1_out, nQ);
  nand nand_4 (nQ, Q, nand_2_out);
endmodule
