// Digital circuit Sys1.dig as structural Verilog
module Sys1 (
  input  A3,
  input  A2,
  input  A1,
  input  A0,
  input  B3,
  input  B2,
  input  B1,
  input  B0,
  output OUT
);

  wire bitcount_1_p5, bitcount_1_p6, bitcount_1_p7, bitcount_2_p5, bitcount_2_p6, bitcount_2_p7, xnor_1_out,
       xnor_2_out, xnor_3_out;

  // bitcount bitcount_1: pin names not known; wires that end beside it: A3, A2, A1, A0, bitcount_1_p5, bitcount_1_p6, bitcount_1_p7
  // bitcount bitcount_2: pin names not known; wires that end beside it: B3, B2, B1, B0, bitcount_2_p5, bitcount_2_p6, bitcount_2_p7
  xnor xnor_1 (xnor_1_out, bitcount_1_p5, bitcount_2_p5);
  xnor xnor_2 (xnor_2_out, bitcount_1_p6, bitcount_2_p6);
  xnor xnor_3 (xnor_3_out, bitcount_1_p7, bitcount_2_p7);
  and and_1 (OUT, xnor_1_out, xnor_2_out, xnor_3_out);
endmodule
