// Digital circuit Sys2.dig as structural Verilog
module Sys2 (
  input  [3:0] A,
  input  [3:0] B,
  output Out
);

  wire [2:0] BC2_1_f, BC2_2_f, xnor_1_out;

  bitcount2 BC2_1 (.X(A), .F(BC2_1_f));
  bitcount2 BC2_2 (.X(B), .F(BC2_2_f));
  // Probe Valor irntermédo A on BC2_1_f
  assign xnor_1_out = ~(BC2_1_f ^ BC2_2_f);  // XNOr xnor_1, 3 bits wide
  // Probe Valor intermédio B on BC2_2_f
  and and_1 (Out, xnor_1_out[0], xnor_1_out[1], xnor_1_out[2]);
endmodule
