// Digital circuit det111.dig as structural Verilog
module det111 (
  input  In,
  input  CLK,
  output Out
);

  wire FF1_q, FF2_q, FF3_q;

  D_FF FF1 (.D(In), .C(CLK), .Q(FF1_q));  // open: nQ
  D_FF FF2 (.D(FF1_q), .C(CLK), .Q(FF2_q));  // open: nQ
  D_FF FF3 (.D(FF2_q), .C(CLK), .Q(FF3_q));  // open: nQ
  and and_1 (Out, FF3_q, FF2_q, FF1_q);
endmodule
