// Digital circuit Acc8.dig as structural Verilog
module Acc8 (
  input  CLK,
  input  [7:0] A,
  input  rst,
  input  en,
  output OVF,
  output [7:0] R
);

  wire [7:0] reg8_1_p5;

  addSub8_ovf addsub8_ovf_1 (.A(A), .B(reg8_1_p5), .OVF(OVF), .R(R));
  // Reg8 reg8_1: pin names not known; wires that end beside it: CLK, R, rst, en, reg8_1_p5
endmodule
