// Digital circuit Add8.dig as structural Verilog
module Add8 (
  input  [7:0] A,
  input  [7:0] B,
  input  Cin,
  output [7:0] S
);

  wire fa_1_p1, fa_1_p3, fa_2_p1, fa_3_p1, fa_4_p1, fa_5_p1, fa_6_p1, fa_7_p1;

  // FA fa_1: pin names not known; wires that end beside it: fa_1_p1, B[7], fa_1_p3, A[7], S[7]
  // FA fa_2: pin names not known; wires that end beside it: fa_2_p1, B[6], fa_1_p1, A[6], S[6]
  // FA fa_3: pin names not known; wires that end beside it: fa_3_p1, B[5], fa_2_p1, A[5], S[5]
  // FA fa_4: pin names not known; wires that end beside it: fa_4_p1, B[4], fa_3_p1, A[4], S[4]
  // FA fa_5: pin names not known; wires that end beside it: fa_5_p1, B[3], fa_4_p1, A[3], S[3]
  // FA fa_6: pin names not known; wires that end beside it: fa_6_p1, B[2], fa_5_p1, A[2], S[2]
  // FA fa_7: pin names not known; wires that end beside it: fa_7_p1, B[1], fa_6_p1, A[1], S[1]
  // FA fa_8: pin names not known; wires that end beside it: Cin, B[0], fa_7_p1, A[0], S[0], fa_1_p3
endmodule
