// Digital circuit AddSub8.dig as structural Verilog
module AddSub8 (
  input  [7:0] B,
  input  AS,
  input  [7:0] A,
  output [7:0] R
);

  wire [7:0] xor_1_out;

  xor xor_1 (xor_1_out[7], AS, B[7]);
  xor xor_2 (xor_1_out[6], AS, B[6]);
  xor xor_3 (xor_1_out[5], AS, B[5]);
  xor xor_4 (xor_1_out[4], AS, B[4]);
  xor xor_5 (xor_1_out[3], AS, B[3]);
  xor xor_6 (xor_1_out[2], AS, B[2]);
  xor xor_7 (xor_1_out[1], AS, B[1]);
  xor xor_8 (xor_1_out[0], AS, B[0]);
  Add8 add8_1 (.A(A), .B(xor_1_out), .Cin(AS), .S(R));
endmodule
