// Digital circuit Acc8-seq_Q9.dig as structural Verilog
module Acc8_seq_Q9 (
  input  CLK,
  input  rst,
  input  en,
  output OVF,
  output [7:0] R
);

  wire not_1_out;
  wire [3:0] counter_1_out;
  wire [7:0] multiplexer_1_out, rom_1_d;

  Counter #(.Bits(4)) counter_1 (.en(en), .C(CLK), .clr(rst), .out(counter_1_out));  // open: ovf
  ROM #(.AddrBits(4), .Bits(8)) rom_1 (.A(counter_1_out), .sel(en), .D(rom_1_d));
  not not_1 (not_1_out, rom_1_d[7]);
  Multiplexer #(.Bits(8)) multiplexer_1 (.sel(not_1_out), .in_0({8{1'b0}}), .in_1(rom_1_d), .out(multiplexer_1_out));
  Acc8 acc8_1 (.CLK(CLK), .A(multiplexer_1_out), .rst(rst), .en(en), .OVF(OVF), .R(R));

  // Notes on the sheet:
  //   contents of rom_1 (hex, n*v repeats v):
  //   1,97,1,97,1,97,1,97,1,1,1,1,1,1,1,11
endmodule
