// Digital circuit Acc8-smem.dig as structural Verilog
module Acc8_smem (
  input  clk,
  input  [7:0] ADDR,
  input  ld,
  input  rst,
  input  en,
  output [7:0] R,
  output OVF
);

  wire and_1_out;
  wire [7:0] counterpreset_1_out, smem_1_p3;

  CounterPreset #(.Bits(8)) counterpreset_1 (
    .en(en), .C(clk), .dir(1'b0), .in(ADDR), .ld(ld), .clr(rst), .out(counterpreset_1_out));  // open: ovf
  // smem smem_1: pin names not known; wires that end beside it: counterpreset_1_out, en, smem_1_p3
  and and_1 (and_1_out, en, ~ld);  // And
  Acc8 acc8_1 (.CLK(clk), .A(smem_1_p3), .rst(rst), .en(and_1_out), .OVF(OVF), .R(R));

  // Notes on the sheet:
  //   Insira aqui o componente Acc8
endmodule
