// Digital circuit Add8_Picasso.dig as structural Verilog
module Add8_Picasso (
  input  [7:0] B,
  input  [7:0] A,
  output [7:0] S
);

  wire FA1_p1, FA2_p1, FA3_p1, FA4_p1, FA5_p1, FA6_p1, FA7_p1, FA7_p3;

  // FA FA7: pin names not known; wires that end beside it: FA7_p1, B[7], FA7_p3, A[7], S[7]
  // FA FA6: pin names not known; wires that end beside it: FA6_p1, B[6], FA7_p1, A[6], S[6]
  // FA FA5: pin names not known; wires that end beside it: FA5_p1, B[5], FA6_p1, A[5], S[5]
  // FA FA4: pin names not known; wires that end beside it: FA4_p1, B[4], FA5_p1, A[4], S[4]
  // FA FA3: pin names not known; wires that end beside it: FA3_p1, FA7_p3, B[3], FA4_p1, A[3], S[3]
  // FA FA2: pin names not known; wires that end beside it: FA2_p1, B[2], FA3_p1, A[2], S[2]
  // FA FA1: pin names not known; wires that end beside it: FA1_p1, B[1], FA2_p1, A[1], S[1]
  // FA FA0: pin names not known; wires that end beside it: 1'b0, B[0], FA1_p1, A[0], S[0]
endmodule
