// Digital circuit addSub8-ovf.dig as structural Verilog
module addSub8_ovf (
  input  [7:0] A,
  input  [7:0] B,
  output OVF,
  output [7:0] R
);

  AddSub8 addsub8_1 (.B(B), .AS(1'b0), .A(A), .R(R));
  det_OVF det_ovf_1 (.AS(1'b0), .sA(A[7]), .sB(B[7]), .sR(R[7]), .OVF(OVF));
endmodule
